# Fritzing sketch schema (saved by Fritzing 0.9.3b)

parts:
  U1 = LuaNode32 / ESP32
  SIM800L_BO1 = SIM800L BO
  C1 = Capacitor Polarized [package=panasonic_d]
  U2 = LIPO-110mAh [package=lipo-110]
  MIC1 = Microphone
  Součástka1 = Solar Cell
  TP1 = TP4056 [chip_label=TP4056 package="DIP (Dual Inline) [THT]"]
  Součástka2 = INA219 High Side DC Current Sensor Breakout [part_number=904]
  U3 = Mini-360 DC-DC Buck converter [package=THT]
  D1 = Zener Diode [part_number=1N4732A breakdown_voltage=3.6V package="Melf DO-213 AB [SMD]"]
  U4 = MPC1700 [package=sot23-3]
  C2 = Electrolytic Capacitor [capacitance=1000μF package="1010 [SMD, electrolytic]"]
  C3 = Capacitor [package=cap-pth-small2]
  Součástka3 = Adafruit SHT31-D Sensirion Temperature/Humidity Sensor [part_number="Adafruit #2857"]
  Součástka4 = Adafruit SHT31-D Sensirion Temperature/Humidity Sensor [part_number="Adafruit #2857"]
  Součástka5 = Adafruit SHT31-D Sensirion Temperature/Humidity Sensor [part_number="Adafruit #2857"]
  Součástka6 = Adafruit MMA8451 Accelerometer [part_number="Adafruit #2019"]
  Součástka7 = Adafruit MMA8451 Accelerometer [part_number="Adafruit #2019"]
  Součástka8 = Adafruit MMA8451 Accelerometer [part_number="Adafruit #2019"]

nets:
  N1: U1.D14, Součástka6.SA0
  N2: U1.D12, Součástka8.SA0
  N3: U1.D13, Součástka7.SA0
  GND: U1.GND, U2.-, TP1.pin5, Součástka2.GND, U4.GND, C2.-, C3.1, Součástka3.GND, Součástka4.GND, Součástka5.GND
  VIN: U1.3V3, Součástka2.VCC, U4.OUT, Součástka3.VIN, Součástka4.VIN, Součástka5.VIN
  N4: U1.RX2, SIM800L_BO1.pin_5
  N5: U1.TX2, SIM800L_BO1.pin_4
  N6: U1.D5, Součástka5.ADDR
  N7: U1.D18, Součástka4.ADDR
  N8: U1.D19, Součástka3.ADDR
  N9: U1.D21, Součástka2.SDA, Součástka3.SDA, Součástka4.SDA, Součástka5.SDA
  N10: U1.D22, Součástka2.SCL, Součástka3.SCL, Součástka4.SCL, Součástka5.SCL
  N11: SIM800L_BO1.PIN2, C1.+, TP1.pin3
  N12: SIM800L_BO1.pin_6, C1.-, TP1.pin6
  N13: SIM800L_BO1.pin_9, MIC1.pin2
  N14: SIM800L_BO1.pin_10, MIC1.pin1
  N15: U2.+, TP1.pin4, U4.IN, C2.+, C3.2
  N16: Součástka1.+, D1.anode
  N17: Součástka1.-, U3.IN-
  N18: TP1.pin1, Součástka2.VIN-
  N19: TP1.pin2, U3.OUT-
  N20: Součástka2.VIN+, U3.OUT+
  N21: U3.IN+, D1.cathode
  N22: Součástka6.SDA, Součástka7.SDA, Součástka8.SDA
  N23: Součástka6.SCL, Součástka7.SCL, Součástka8.SCL
  GND_2: Součástka6.GND, Součástka7.GND, Součástka8.GND
  VIN_2: Součástka6.VIN, Součástka7.VIN, Součástka8.VIN

custom parts:
  LuaNode32 / ESP32: ESP32 based LuaNode32
  TP4056: A DIP stand-in part for whatever IC you want. With 6 pins on a 300mil dual inline package (DIP) footprint.
  INA219 High Side DC Current Sensor Breakout: This breakout board will solve all your power-monitoring problems. Instead of struggling with two multimeters, you can just use the handy INA219B chip on this breakout to both measure both the high side voltage and DC current draw over I2C with 1% precision. Most current-measuring devices such as our current panel meter are only good for low side measuring. That means that unless you want to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
  Mini-360 DC-DC Buck converter: Mini-360 DC-DC Buck converter. Tiny buck step down voltage converter, input voltage 4.75 to 23V output 1 to 17V adjustable. Available from ebay and the like.
  MPC1700: Small package LDO
  Adafruit SHT31-D Sensirion Temperature/Humidity Sensor: Sensirion Temperature/Humidity sensors are some of the finest & highest-accuracy devices you can get. And, finally we have some that have a true I2C interface for easy reading. The SHT31-D sensor has an excellent ±2% relative humidity and ±0.3°C accuracy for most uses. Unlike earlier SHT sensors, this sensor has a true I2C interface, and (bonus!) even with two address options. It also is 3V or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
  Adafruit MMA8451 Accelerometer: So many accelerometers and so little time! We've expanded our accelerometer selection even more with this high-precision and inexpensive MMA8451 Triple-Axis Accelerometer w/ 14-bit ADC. You can detect motion, tilt and basic orientation with a digital accelerometer - and the MMA8451 is a great accelerometer to start with. It has a wide usage range, from +-2g up to +-8g yet is easy to use with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
